// Logisim project processor.circ as structural Verilog: 5 circuits, main circuit Processor Main
module ALU (
  input  [2:0] Shamt,
  input  [15:0] A,
  input  [15:0] B,
  input  [3:0] ALUOp,
  output zero,
  output less_than,
  output [15:0] ALU_out
);

  wire comparator_1_lt;
  wire [3:0] bit_extender_1_out;
  wire [15:0] adder_1_out, and_1_out, not_1_out, not_2_out, or_1_out, shifter_1_out, shifter_2_out,
       subtractor_1_out;

  assign bit_extender_1_out = {{1{1'b0}}, Shamt};  // Bit_Extender bit_extender_1
  assign or_1_out = A | B;  // OR_Gate or_1, 16 bits wide
  assign not_1_out = ~B;  // NOT_Gate not_1, 16 bits wide
  Adder #(.width(16)) adder_1 (.a(A), .b(B), .out(adder_1_out));  // open: cin, cout
  Subtractor #(.width(16)) subtractor_1 (.a(A), .b(B), .out(subtractor_1_out));  // open: bin, bout
  Shifter #(.width(16), .shift("lr")) shifter_1 (.in(A), .\dist (bit_extender_1_out), .out(shifter_1_out));
  Shifter #(.width(16)) shifter_2 (.in(A), .\dist (bit_extender_1_out), .out(shifter_2_out));
  assign not_2_out = ~A;  // NOT_Gate not_2, 16 bits wide
  assign and_1_out = A & not_2_out;  // AND_Gate and_1, 16 bits wide
  Multiplexer #(.select(4), .width(16), .enable("false")) multiplexer_1 (
    .in0(or_1_out), .in1(not_1_out), .in2(adder_1_out), .in3(adder_1_out), .in4(subtractor_1_out),
    .in5(shifter_1_out), .in6(shifter_2_out), .in7(adder_1_out), .in8(adder_1_out), .in9(subtractor_1_out),
    .in10(subtractor_1_out), .in11(and_1_out), .in12(and_1_out), .in13(and_1_out), .in14(and_1_out),
    .in15(and_1_out), .out(ALU_out), .sel(ALUOp));
  Comparator #(.width(16)) comparator_1 (.a(and_1_out), .b(ALU_out), .eq(zero), .lt(comparator_1_lt));  // open: gt
  and and_2 (less_than, zero, comparator_1_lt);
endmodule

module sign_extender (
  input  [5:0] Immediate_Value,
  output [15:0] Output
);


  assign Output = {{11{Immediate_Value[5]}}, Immediate_Value[4:0]};
endmodule

module Processor_Main (
  input  Reset
);

  wire alu_1_less_than, alu_1_zero, ALUSrc, and_1_out, and_2_out, ble_on, branch, Branch_Available, jal, jr,
       jump, MemRead, MemtoReg, MemWrite, or_1_out, RegDst, RegWrite, System_Clock, User_Input, Write_Output;
  wire [2:0] multiplexer_1_out, multiplexer_3_out, regfile_1_p6;
  wire [3:0] opcode;
  wire [6:0] Keyboard_Input;
  wire [11:0] Instr_Bits_0_11;
  wire [15:0] alu_1_alu_out, Immediate, jal_write_data, multiplexer_4_out, multiplexer_6_out,
       multiplexer_7_out, PC_Computation_Unit_pcout, PC_q, ram_1_data, regfile_1_p9, Register_Write_Data,
       rs_register_data;

  Clock clock_1 (.out(System_Clock));
  Register #(.width(16)) PC (.D(PC_Computation_Unit_pcout), .Q(PC_q), .clk(System_Clock), .clr(Reset));  // open: en
  Multiplexer #(.width(3), .enable("false")) multiplexer_1 (
    .in0(multiplexer_3_out), .in1(3'b111), .out(multiplexer_1_out), .sel(jal));
  PC_Computation PC_Computation_Unit (
    .PC(PC_q), .Instruction_Bits_0_11(Instr_Bits_0_11), .Immediate(Immediate),
    .rs_register(rs_register_data), .Branch_Available(Branch_Available), .JAL(jump), .jump(jal),
    .PCOut(PC_Computation_Unit_pcout), .jr(jr), .Jal_write_data(jal_write_data));
  // regfile regfile_1: pin names not known; wires that end beside it: Register_Write_Data, System_Clock, Reset, RegWrite, multiplexer_1_out, regfile_1_p6, Instr_Bits_0_11[8:6], rs_register_data, regfile_1_p9
  Multiplexer #(.width(3), .enable("false")) multiplexer_2 (
    .in0(Instr_Bits_0_11[11:9]), .in1(3'b111), .out(regfile_1_p6), .sel(jr));
  ROM #(.addrWidth(16), .dataWidth(16)) rom_1 (.addr(PC_q), .data({opcode, Instr_Bits_0_11}));  // open: sel
  sign_extender sign_extender_1 (.Immediate_Value(Instr_Bits_0_11[5:0]), .Output(Immediate));
  Multiplexer #(.width(3), .enable("false")) multiplexer_3 (
    .in0(Instr_Bits_0_11[8:6]), .in1(Instr_Bits_0_11[5:3]), .out(multiplexer_3_out), .sel(RegDst));
  Multiplexer #(.width(16), .enable("false")) multiplexer_4 (
    .in0(regfile_1_p9), .in1(Immediate), .out(multiplexer_4_out), .sel(ALUSrc));
  Keyboard keyboard_1 (.clk(System_Clock), .re(User_Input), .clr(Reset), .data(Keyboard_Input));  // open: avail
  and and_1 (and_1_out, branch, alu_1_zero);
  ALU alu_1 (
    .Shamt(Instr_Bits_0_11[2:0]), .A(rs_register_data), .B(multiplexer_4_out), .ALUOp(opcode),
    .zero(alu_1_zero), .less_than(alu_1_less_than), .ALU_out(alu_1_alu_out));
  Multiplexer #(.enable("false")) multiplexer_5 (
    .in0(and_1_out), .in1(and_2_out), .out(Branch_Available), .sel(ble_on));
  and and_2 (and_2_out, branch, or_1_out);
  or or_1 (or_1_out, alu_1_zero, alu_1_less_than);
  RAM #(.addrWidth(16), .dataWidth(16), .bus("separate")) ram_1 (
    .addr(alu_1_alu_out), .din(regfile_1_p9), .data(ram_1_data), .str(MemWrite), .clk(System_Clock),
    .ld(MemRead));  // open: sel, clr
  TTY tty_1 (.data(rs_register_data[6:0]), .clk(System_Clock), .we(Write_Output), .clr(Reset));
  Multiplexer #(.width(16), .enable("false")) multiplexer_6 (
    .in0(alu_1_alu_out), .in1(ram_1_data), .out(multiplexer_6_out), .sel(MemtoReg));
  Multiplexer #(.width(16), .enable("false")) multiplexer_7 (
    .in0(multiplexer_6_out), .in1({{9{1'b0}}, Keyboard_Input}), .out(multiplexer_7_out), .sel(User_Input));
  Instruction_Decoder instruction_decoder_1 (
    .opcode(opcode), .RegWrite(RegWrite), .RegDst(RegDst), .ALUSrc(ALUSrc), .MemtoReg(MemtoReg),
    .MemRead(MemRead), .MemWrite(MemWrite), .ble_on(ble_on), .Branch(branch), .jal(jal), .jump(jump),
    .jr(jr), .User_Input(User_Input), .Write_Output(Write_Output));
  Multiplexer #(.width(16), .enable("false")) multiplexer_8 (
    .in0(multiplexer_7_out), .in1(jal_write_data), .out(Register_Write_Data), .sel(jal));

  // Other names for the same wires on the sheet: shamt[2:0] = Instr_Bits_0_11[2:0]; rd[2:0] = Instr_Bits_0_11[5:3];
  //   rt[2:0] = Instr_Bits_0_11[8:6]; rs[2:0] = Instr_Bits_0_11[11:9]
endmodule

module Instruction_Decoder (
  input  [3:0] opcode,
  output RegWrite,
  output RegDst,
  output ALUSrc,
  output MemtoReg,
  output MemRead,
  output MemWrite,
  output ble_on,
  output Branch,
  output jal,
  output jump,
  output jr,
  output User_Input,
  output Write_Output
);

  wire add_R_out, addi_I_out, beq_I_out, not_R_out, or_R_out, shl_R_out, shr_R_out, sub_R_out;

  and or_R (or_R_out, ~opcode[0], ~opcode[1], ~opcode[2], ~opcode[3]);  // AND_Gate
  and not_R (not_R_out, opcode[0], ~opcode[1], ~opcode[2], ~opcode[3]);  // AND_Gate
  and add_R (add_R_out, ~opcode[0], opcode[1], ~opcode[2], ~opcode[3]);  // AND_Gate
  and addi_I (addi_I_out, opcode[0], opcode[1], ~opcode[2], ~opcode[3]);  // AND_Gate
  and sub_R (sub_R_out, ~opcode[0], ~opcode[1], opcode[2], ~opcode[3]);  // AND_Gate
  and shr_R (shr_R_out, opcode[0], ~opcode[1], opcode[2], ~opcode[3]);  // AND_Gate
  and shl_R (shl_R_out, ~opcode[0], opcode[1], opcode[2], ~opcode[3]);  // AND_Gate
  and lw_I (MemRead, opcode[0], opcode[1], opcode[2], ~opcode[3]);  // AND_Gate
  and sw_I (MemWrite, ~opcode[0], ~opcode[1], ~opcode[2], opcode[3]);  // AND_Gate
  and ble_I (ble_on, opcode[0], ~opcode[1], ~opcode[2], opcode[3]);  // AND_Gate
  and beq_I (beq_I_out, ~opcode[0], opcode[1], ~opcode[2], opcode[3]);  // AND_Gate
  and jal_J (jal, opcode[0], opcode[1], ~opcode[2], opcode[3]);  // AND_Gate
  and j_J (jump, ~opcode[0], ~opcode[1], opcode[2], opcode[3]);  // AND_Gate
  and jr_R (jr, opcode[0], ~opcode[1], opcode[2], opcode[3]);  // AND_Gate
  and input_R (User_Input, ~opcode[0], opcode[1], opcode[2], opcode[3]);  // AND_Gate
  and output_R (Write_Output, opcode[0], opcode[1], opcode[2], opcode[3]);
  or or_1 (Branch, ble_on, beq_I_out);
  or RWr (RegWrite, or_R_out, not_R_out, add_R_out, addi_I_out, sub_R_out, shr_R_out, shl_R_out, MemRead, jal, User_Input);
  or or_2 (RegDst, or_R_out, not_R_out, add_R_out, sub_R_out, shr_R_out, shl_R_out, User_Input);
  or or_3 (ALUSrc, addi_I_out, MemRead, MemWrite);

  assign MemtoReg = MemRead;
endmodule

module PC_Computation (
  input  [15:0] PC,
  input  jr,
  input  Branch_Available,
  input  [11:0] Instruction_Bits_0_11,
  input  JAL,
  input  jump,
  input  [15:0] Immediate,
  input  [15:0] rs_register,
  output [15:0] PCOut,
  output [15:0] Jal_write_data
);

  wire or_1_out;
  wire [15:0] adder_2_out, multiplexer_1_out, multiplexer_2_out;

  Adder #(.width(16)) adder_1 (.a(PC), .b(16'h1), .out(Jal_write_data));  // open: cin, cout
  Adder #(.width(16)) adder_2 (.a(Jal_write_data), .b(Immediate), .out(adder_2_out));  // open: cin, cout
  Multiplexer #(.width(16), .enable("false")) multiplexer_1 (
    .in0(Jal_write_data), .in1(adder_2_out), .out(multiplexer_1_out), .sel(Branch_Available));
  Multiplexer #(.width(16), .enable("false")) multiplexer_2 (
    .in0(multiplexer_1_out), .in1({PC[15:12], Instruction_Bits_0_11}), .out(multiplexer_2_out), .sel(or_1_out));
  or or_1 (or_1_out, JAL, jump);
  Multiplexer #(.width(16), .enable("false")) multiplexer_3 (
    .in0(multiplexer_2_out), .in1(rs_register), .out(PCOut), .sel(jr));
endmodule
